// Logisim project CustomAdder.circ as structural Verilog: 2 circuits, main circuit CustomAdder
module CustomAdder (
  input  [7:0] FirstOperand,
  input  [7:0] SecondOperand,
  output [7:0] Result
);

  Adder adder_1 (.a(FirstOperand), .b(SecondOperand), .out(Result), .cin(1'b0));  // open: cout

  // Other names for the same wires on the sheet: A[7:0] = FirstOperand; B[7:0] = SecondOperand; C[7:0] = Result
endmodule

module fourBitAdder (
  input  [3:0] FirstOperand,
  input  [3:0] SecondOperand,
  output [3:0] Result,
  output Cout
);

  Adder #(.width(4)) adder_1 (.a(FirstOperand), .b(SecondOperand), .out(Result), .cin(1'b0), .cout(Cout));

  // Other names for the same wires on the sheet: A[3:0] = FirstOperand; B[3:0] = SecondOperand; C[3:0] = Result
endmodule
