// Logisim project CustomCombinationalMultiplier.circ as structural Verilog: 4 circuits, main circuit CustomMultiplierCombinationalMessy
module CustomMultiplierCombinationalMessy (
  input  [7:0] FirstOperand,
  input  [7:0] SecondOperand,
  input  Clock,
  output [7:0] Result,
  output Done,
  output p0,
  output p1,
  output p2,
  output p3,
  output p4,
  output p5,
  output p6,
  output p7,
  output p8,
  output p9,
  output p10,
  output p11,
  output p12,
  output p13,
  output p14,
  output p15
);

  wire carry, carry1, carry2;
  wire [3:0] fourbitmultiplier_3_p4;
  wire [7:0] adder_1_out, fourbitmultiplier_1_p0, fourbitmultiplier_2_p0, fourbitmultiplier_4_p0;
  wire [7:4] adder_2_out;

  fourBitMultiplier fourbitmultiplier_1 (
    .FirstOperand(FirstOperand[3:0]), .SecondOperand(SecondOperand[7:4]), .p0(fourbitmultiplier_1_p0[0]),
    .p1(fourbitmultiplier_1_p0[1]), .p2(fourbitmultiplier_1_p0[2]), .p7(fourbitmultiplier_1_p0[7]),
    .p6(fourbitmultiplier_1_p0[6]), .p5(fourbitmultiplier_1_p0[5]), .p4(fourbitmultiplier_1_p0[4]),
    .p3(fourbitmultiplier_1_p0[3]));
  fourBitMultiplier fourbitmultiplier_2 (
    .FirstOperand(FirstOperand[7:4]), .SecondOperand(SecondOperand[3:0]), .p0(fourbitmultiplier_2_p0[0]),
    .p1(fourbitmultiplier_2_p0[1]), .p2(fourbitmultiplier_2_p0[2]), .p7(fourbitmultiplier_2_p0[7]),
    .p6(fourbitmultiplier_2_p0[6]), .p5(fourbitmultiplier_2_p0[5]), .p4(fourbitmultiplier_2_p0[4]),
    .p3(fourbitmultiplier_2_p0[3]));
  fourBitMultiplier fourbitmultiplier_3 (
    .FirstOperand(FirstOperand[3:0]), .SecondOperand(SecondOperand[3:0]), .p0(p0), .p1(p1), .p2(p2),
    .p7(fourbitmultiplier_3_p4[3]), .p6(fourbitmultiplier_3_p4[2]), .p5(fourbitmultiplier_3_p4[1]),
    .p4(fourbitmultiplier_3_p4[0]), .p3(p3));
  Adder adder_1 (.a(fourbitmultiplier_1_p0), .b(fourbitmultiplier_2_p0), .out(adder_1_out), .cin(1'b0), .cout(carry1));
  Adder adder_2 (
    .a({4'b0000, fourbitmultiplier_3_p4}), .b(adder_1_out), .out({adder_2_out, p7, p6, p5, p4}), .cin(1'b0),
    .cout(carry2));
  Adder adder_3 (
    .a(fourbitmultiplier_4_p0), .b({3'b000, carry1, adder_2_out}),
    .out({p15, p14, p13, p12, p11, p10, p9, p8}), .cin(1'b0), .cout(carry));
  fourBitMultiplier fourbitmultiplier_4 (
    .FirstOperand(FirstOperand[7:4]), .SecondOperand(SecondOperand[7:4]), .p0(fourbitmultiplier_4_p0[0]),
    .p1(fourbitmultiplier_4_p0[1]), .p2(fourbitmultiplier_4_p0[2]), .p7(fourbitmultiplier_4_p0[7]),
    .p6(fourbitmultiplier_4_p0[6]), .p5(fourbitmultiplier_4_p0[5]), .p4(fourbitmultiplier_4_p0[4]),
    .p3(fourbitmultiplier_4_p0[3]));

  assign Done = 1'b1;

  // Other names for the same wires on the sheet: A[7:0] = FirstOperand; a0 = FirstOperand[0]; a1 = FirstOperand[1];
  //   a2 = FirstOperand[2]; a3 = FirstOperand[3]; B[7:0] = SecondOperand; b0 = SecondOperand[0];
  //   b1 = SecondOperand[1]; b2 = SecondOperand[2]; b3 = SecondOperand[3]; a4 = FirstOperand[4]; a5 = FirstOperand[5];
  //   a6 = FirstOperand[6]; a7 = FirstOperand[7]; b4 = SecondOperand[4]; b5 = SecondOperand[5]; b6 = SecondOperand[6];
  //   b7 = SecondOperand[7]; C[7:0] = Result; clk = Clock
endmodule

module fourBitMultiplier (
  input  [3:0] FirstOperand,
  input  [3:0] SecondOperand,
  output p0,
  output p1,
  output p2,
  output p7,
  output p6,
  output p5,
  output p4,
  output p3
);

  wire [2:0] and_2_out;
  wire [3:0] and_5_out, and_9_out, and_12_out;
  wire [3:1] fourbitadder_1_result, fourbitadder_2_result;
  wire [3:3] fourbitadder_1_cout, fourbitadder_2_cout;

  and and_1 (p0, SecondOperand[0], FirstOperand[0]);
  and and_2 (and_2_out[0], SecondOperand[0], FirstOperand[1]);
  and and_3 (and_2_out[1], SecondOperand[0], FirstOperand[2]);
  and and_4 (and_2_out[2], SecondOperand[0], FirstOperand[3]);
  fourBitAdder fourbitadder_1 (
    .FirstOperand(and_5_out), .SecondOperand({1'b0, and_2_out}), .Result({fourbitadder_1_result, p1}),
    .Cout(fourbitadder_1_cout[3]));
  and and_5 (and_5_out[0], SecondOperand[1], FirstOperand[0]);
  and and_6 (and_5_out[1], SecondOperand[1], FirstOperand[1]);
  fourBitAdder fourbitadder_2 (
    .FirstOperand(and_9_out), .SecondOperand({fourbitadder_1_cout[3], fourbitadder_1_result}),
    .Result({fourbitadder_2_result, p2}), .Cout(fourbitadder_2_cout[3]));
  and and_7 (and_5_out[2], SecondOperand[1], FirstOperand[2]);
  and and_8 (and_5_out[3], SecondOperand[1], FirstOperand[3]);
  and and_9 (and_9_out[0], SecondOperand[2], FirstOperand[0]);
  fourBitAdder fourbitadder_3 (
    .FirstOperand(and_12_out), .SecondOperand({fourbitadder_2_cout[3], fourbitadder_2_result}),
    .Result({p6, p5, p4, p3}), .Cout(p7));
  and and_10 (and_9_out[1], SecondOperand[2], FirstOperand[1]);
  and and_11 (and_9_out[2], SecondOperand[2], FirstOperand[2]);
  and and_12 (and_12_out[0], SecondOperand[3], FirstOperand[0]);
  and and_13 (and_9_out[3], SecondOperand[2], FirstOperand[3]);
  and and_14 (and_12_out[1], SecondOperand[3], FirstOperand[1]);
  and and_15 (and_12_out[2], SecondOperand[3], FirstOperand[2]);
  and and_16 (and_12_out[3], SecondOperand[3], FirstOperand[3]);

  // Other names for the same wires on the sheet: A[3:0] = FirstOperand; a0 = FirstOperand[0]; a1 = FirstOperand[1];
  //   a2 = FirstOperand[2]; a3 = FirstOperand[3]; B[3:0] = SecondOperand; b0 = SecondOperand[0];
  //   b1 = SecondOperand[1]; b2 = SecondOperand[2]; b3 = SecondOperand[3]
endmodule

module customMultiplierCombinational (
  input  [7:0] FirstOperand,
  input  [7:0] SecondOperand,
  input  Clock,
  output [7:0] Result,
  output Done
);

  CustomMultiplierCombinationalMessy custommultipliercombinationalmessy_1 (
    .FirstOperand(FirstOperand), .SecondOperand(SecondOperand), .Clock(1'b0), .p0(Result[0]), .p1(Result[1]),
    .p2(Result[2]), .p3(Result[3]), .p4(Result[4]), .p5(Result[5]), .p6(Result[6]), .p7(Result[7]));  // open: Result, Done, p8, p9, p10, p11, p12, p13, p14, p15

  assign Done = 1'b1;

  // Other names for the same wires on the sheet: A[7:0] = FirstOperand; B[7:0] = SecondOperand; C[7:0] = Result;
  //   clk = Clock
endmodule

module MyAdder (
  input  [7:0] FirstOperand,
  input  [7:0] SecondOperand,
  output [7:0] Result
);

  Adder adder_1 (.a(FirstOperand), .b(SecondOperand), .out(Result), .cin(1'b0));  // open: cout

  // Other names for the same wires on the sheet: A[7:0] = FirstOperand; B[7:0] = SecondOperand; C[7:0] = Result
endmodule
