// Logisim project MatrixCalculation.circ as structural Verilog: 1 circuit, main circuit MAC
module MAC (
  input  [31:0] A,
  input  [31:0] X,
  input  [31:0] B,
  input  clock,
  output [31:0] Result,
  output Done
);

  wire [7:0] custommultipliercombinational_1_result, custommultipliercombinational_2_result,
       custommultipliercombinational_3_result, custommultipliercombinational_4_result,
       custommultipliercombinational_5_result, custommultipliercombinational_6_result,
       custommultipliercombinational_7_result, custommultipliercombinational_8_result, myadder_1_result,
       myadder_2_result, myadder_3_result, myadder_4_result;

  customMultiplierCombinational custommultipliercombinational_1 (
    .FirstOperand(A[23:16]), .SecondOperand(X[7:0]), .Clock(clock),
    .Result(custommultipliercombinational_1_result));  // open: Done
  customMultiplierCombinational custommultipliercombinational_2 (
    .FirstOperand(A[31:24]), .SecondOperand(X[23:16]), .Clock(clock),
    .Result(custommultipliercombinational_2_result));  // open: Done
  customMultiplierCombinational custommultipliercombinational_3 (
    .FirstOperand(A[23:16]), .SecondOperand(X[15:8]), .Clock(clock),
    .Result(custommultipliercombinational_3_result));  // open: Done
  customMultiplierCombinational custommultipliercombinational_4 (
    .FirstOperand(A[31:24]), .SecondOperand(X[31:24]), .Clock(clock),
    .Result(custommultipliercombinational_4_result));  // open: Done
  customMultiplierCombinational custommultipliercombinational_5 (
    .FirstOperand(A[7:0]), .SecondOperand(X[7:0]), .Clock(clock),
    .Result(custommultipliercombinational_5_result));  // open: Done
  customMultiplierCombinational custommultipliercombinational_6 (
    .FirstOperand(A[15:8]), .SecondOperand(X[23:16]), .Clock(clock),
    .Result(custommultipliercombinational_6_result));  // open: Done
  customMultiplierCombinational custommultipliercombinational_7 (
    .FirstOperand(A[7:0]), .SecondOperand(X[15:8]), .Clock(clock),
    .Result(custommultipliercombinational_7_result));  // open: Done
  customMultiplierCombinational custommultipliercombinational_8 (
    .FirstOperand(A[15:8]), .SecondOperand(X[31:24]), .Clock(clock),
    .Result(custommultipliercombinational_8_result));  // open: Done
  MyAdder myadder_1 (
    .FirstOperand(custommultipliercombinational_1_result),
    .SecondOperand(custommultipliercombinational_2_result), .Result(myadder_1_result));
  MyAdder myadder_2 (
    .FirstOperand(custommultipliercombinational_3_result),
    .SecondOperand(custommultipliercombinational_4_result), .Result(myadder_2_result));
  MyAdder myadder_3 (
    .FirstOperand(custommultipliercombinational_5_result),
    .SecondOperand(custommultipliercombinational_6_result), .Result(myadder_3_result));
  MyAdder myadder_4 (
    .FirstOperand(custommultipliercombinational_7_result),
    .SecondOperand(custommultipliercombinational_8_result), .Result(myadder_4_result));
  MyAdder myadder_5 (.FirstOperand(myadder_3_result), .SecondOperand(B[7:0]), .Result(Result[7:0]));
  MyAdder myadder_6 (.FirstOperand(myadder_4_result), .SecondOperand(B[15:8]), .Result(Result[15:8]));
  MyAdder myadder_7 (.FirstOperand(myadder_1_result), .SecondOperand(B[23:16]), .Result(Result[23:16]));
  MyAdder myadder_8 (.FirstOperand(myadder_2_result), .SecondOperand(B[31:24]), .Result(Result[31:24]));

  assign Done = 1'b1;

  // Other names for the same wires on the sheet: A_1_1[7:0] = A[7:0]; A_1_2[7:0] = A[15:8]; A_2_1[7:0] = A[23:16];
  //   A_2_2[7:0] = A[31:24]; B_1_1[7:0] = B[7:0]; B_1_2[7:0] = B[15:8]; B_2_1[7:0] = B[23:16]; B_2_2[7:0] = B[31:24];
  //   clk = clock; Result_1_1[7:0] = Result[7:0]; Result_1_2[7:0] = Result[15:8]; Result_2_1[7:0] = Result[23:16];
  //   Result_2_2[7:0] = Result[31:24]; X_1_1[7:0] = X[7:0]; X_1_2[7:0] = X[15:8]; X_2_1[7:0] = X[23:16];
  //   X_2_2[7:0] = X[31:24]

  // Notes on the sheet:
  //   Please don't change places of inputs and outputs
endmodule
