// Logisim project 4bitAdder.circ as structural Verilog: 1 circuit, main circuit Adder_4bit
module Adder_4bit (
  input  a0,
  input  b0,
  input  a1,
  input  b1,
  input  a2,
  input  b2,
  input  a3,
  input  b3,
  output s0,
  output s1,
  output s2,
  output s3,
  output C_out
);

  wire fulladder_1_c_out, fulladder_2_c_out, fulladder_3_c_out;

  fullAdder fulladder_1 (.c_in(1'b0), .a(a0), .b(b0), .sum(s0), .c_out(fulladder_1_c_out));
  fullAdder fulladder_2 (.c_in(fulladder_1_c_out), .a(a1), .b(b1), .sum(s1), .c_out(fulladder_2_c_out));
  fullAdder fulladder_3 (.c_in(fulladder_2_c_out), .a(a2), .b(b2), .sum(s2), .c_out(fulladder_3_c_out));
  fullAdder fulladder_4 (.c_in(fulladder_3_c_out), .a(a3), .b(b3), .sum(s3), .c_out(C_out));
endmodule
