// Logisim project 4bitMultiplier.circ as structural Verilog: 1 circuit, main circuit multiplier_4bit
module multiplier_4bit (
  input  a3,
  input  a2,
  input  a1,
  input  a0,
  input  b3,
  input  b2,
  input  b1,
  input  b0,
  output m7,
  output m6,
  output m5,
  output m4,
  output m3,
  output m2,
  output m1,
  output m
);

  wire adder_4bit_1_c_out, adder_4bit_1_s0, adder_4bit_1_s1, adder_4bit_1_s2, adder_4bit_1_s3, and_1_out,
       and_2_out, and_3_out, and_4_out, clock_1_out, d_ff_1_q, d_ff_3_q, d_ff_5_q, d_ff_7_q, d_ff_13_q,
       multiplexer_1_out, multiplexer_2_out, multiplexer_3_out, multiplexer_4_out;

  Clock clock_1 (.out(clock_1_out));
  D_Flip_Flop d_ff_1 (.D(a3), .clk(clock_1_out), .Q(d_ff_1_q));  // open: Qn, preset, reset
  D_Flip_Flop d_ff_2 (.D(adder_4bit_1_c_out), .clk(clock_1_out), .Q(m7));  // open: Qn, preset, reset
  D_Flip_Flop d_ff_3 (.D(a2), .clk(clock_1_out), .Q(d_ff_3_q));  // open: Qn, preset, reset
  and and_1 (and_1_out, d_ff_1_q, d_ff_13_q);
  D_Flip_Flop d_ff_4 (.D(adder_4bit_1_s3), .clk(clock_1_out), .Q(m6));  // open: Qn, preset, reset
  and and_2 (and_2_out, d_ff_3_q, d_ff_13_q);
  D_Flip_Flop d_ff_5 (.D(a1), .clk(clock_1_out), .Q(d_ff_5_q));  // open: Qn, preset, reset
  Adder_4bit adder_4bit_1 (
    .a0(and_4_out), .b0(m4), .a1(and_3_out), .b1(m5), .a2(and_2_out), .b2(m6), .a3(and_1_out), .b3(m7),
    .s0(adder_4bit_1_s0), .s1(adder_4bit_1_s1), .s2(adder_4bit_1_s2), .s3(adder_4bit_1_s3),
    .C_out(adder_4bit_1_c_out));
  D_Flip_Flop d_ff_6 (.D(adder_4bit_1_s2), .clk(clock_1_out), .Q(m5));  // open: Qn, preset, reset
  D_Flip_Flop d_ff_7 (.D(a0), .clk(clock_1_out), .Q(d_ff_7_q));  // open: Qn, preset, reset
  and and_3 (and_3_out, d_ff_5_q, d_ff_13_q);
  D_Flip_Flop d_ff_8 (.D(adder_4bit_1_s1), .clk(clock_1_out), .Q(m4));  // open: Qn, preset, reset
  and and_4 (and_4_out, d_ff_7_q, d_ff_13_q);
  D_Flip_Flop d_ff_9 (.D(adder_4bit_1_s0), .clk(clock_1_out), .Q(m3));  // open: Qn, preset, reset
  Multiplexer multiplexer_1 (.in0(m3), .in1(b3), .out(multiplexer_1_out), .sel(clock_1_out));
  D_Flip_Flop d_ff_10 (.D(multiplexer_1_out), .Q(m2));  // open: clk, Qn, preset, reset
  Multiplexer multiplexer_2 (.in0(m2), .in1(b2), .out(multiplexer_2_out), .sel(clock_1_out));
  D_Flip_Flop d_ff_11 (.D(multiplexer_2_out), .Q(m1));  // open: clk, Qn, preset, reset
  Multiplexer multiplexer_3 (.in0(m1), .in1(b1), .out(multiplexer_3_out), .sel(clock_1_out));
  D_Flip_Flop d_ff_12 (.D(multiplexer_3_out), .Q(m));  // open: clk, Qn, preset, reset
  Multiplexer multiplexer_4 (.in0(m), .in1(b0), .out(multiplexer_4_out), .sel(clock_1_out));
  D_Flip_Flop d_ff_13 (.D(multiplexer_4_out), .Q(d_ff_13_q));  // open: clk, Qn, preset, reset
endmodule
