// Logisim project customFullAdder.circ as structural Verilog: 1 circuit, main circuit fullAdder
module fullAdder (
  input  c_in,
  input  a,
  input  b,
  output sum,
  output c_out
);

  wire and_1_out, and_2_out, xor_1_out;

  xor xor_1 (xor_1_out, a, b);
  and and_1 (and_1_out, a, a);
  xor xor_2 (sum, c_in, xor_1_out);
  and and_2 (and_2_out, c_in, c_in);
  or or_1 (c_out, and_2_out, and_1_out);
endmodule
